// Logisim project processeur_ARO2.circ as structural Verilog: 29 circuits, main circuit main
module main (
);

  wire clk, high_write_en_s, low_write_en_s, processeur_aro2_1_memory_high_byte_o,
       processeur_aro2_1_memory_ldr_data, processeur_aro2_1_memory_low_byte_o,
       processeur_aro2_1_memory_str_data_o, RESET_out, sysclk;
  wire [7:0] rd_data_high_s, rd_data_low_s, wr_data_high_s, wr_data_low_s;
  wire [14:0] memory_addr_s;
  wire [15:0] InstrMemory_data, processeur_aro2_1_instr_addr_o, processeur_aro2_1_memory_wr_data_o, rd_data_s;

  Button RESET (.out(RESET_out));
  Clock #(.highDuration(4), .lowDuration(4)) u_clk (.out(clk));
  Clock u_sysclk (.out(sysclk));
  // Probe on processeur_aro2_1_instr_addr_o
  ROM #(.addrWidth(15), .dataWidth(16)) InstrMemory (
    .addr(processeur_aro2_1_instr_addr_o[15:1]), .data(InstrMemory_data));
  // Probe on InstrMemory_data
  processeur_ARO2 processeur_aro2_1 (
    .instr_data_i(InstrMemory_data), .memory_rd_data_i(rd_data_s), .rst_i(RESET_out), .clk_i(clk),
    .instr_addr_o(processeur_aro2_1_instr_addr_o), .memory_addr_o(memory_addr_s),
    .memory_wr_data_o(processeur_aro2_1_memory_wr_data_o),
    .memory_str_data_o(processeur_aro2_1_memory_str_data_o),
    .memory_ldr_data(processeur_aro2_1_memory_ldr_data),
    .memory_high_byte_o(processeur_aro2_1_memory_high_byte_o),
    .memory_low_byte_o(processeur_aro2_1_memory_low_byte_o));
  RAM #(.addrWidth(15), .databus("bibus")) DataMemoryHigh (
    .addr(memory_addr_s), .we(high_write_en_s), .oe(1'b1), .clk(sysclk), .din(wr_data_high_s),
    .dout(rd_data_high_s));
  RAM #(.addrWidth(15), .databus("bibus")) DataMemoryLow (
    .addr(memory_addr_s), .we(low_write_en_s), .oe(1'b1), .clk(sysclk), .din(wr_data_low_s),
    .dout(rd_data_low_s));
  memory_controller memory_controller_1 (
    .wr_data_i(processeur_aro2_1_memory_wr_data_o), .str_data_i(processeur_aro2_1_memory_str_data_o),
    .ldr_data_i(processeur_aro2_1_memory_ldr_data), .high_byte_i(processeur_aro2_1_memory_high_byte_o),
    .low_byte_i(processeur_aro2_1_memory_low_byte_o), .rd_data_high_i(rd_data_high_s),
    .rd_data_low_i(rd_data_low_s), .rd_data_o(rd_data_s), .high_data_o(wr_data_high_s),
    .low_data_o(wr_data_low_s), .high_write_en_o(high_write_en_s), .low_write_en_o(low_write_en_s));

  // Notes on the sheet:
  //   Attention, votre version de Logisim
  //   ne contient pas de tracker. Si vous
  //   enregistrez votre projet, toutes les
  //   informations du tracker seront
  //   définitivement effacées.
  //   contents of InstrMemory (hex, n*v repeats v):
  //   2005 2102 1842 1d13 e01a 27*0 2206 1e53 d00c 13*0 2004 2180 e7cc
endmodule

module memory_controller (
  input  [15:0] wr_data_i,
  input  str_data_i,
  input  ldr_data_i,
  input  high_byte_i,
  input  low_byte_i,
  input  [7:0] rd_data_high_i,
  input  [7:0] rd_data_low_i,
  output [15:0] rd_data_o,
  output [7:0] high_data_o,
  output [7:0] low_data_o,
  output high_write_en_o,
  output low_write_en_o
);

  wire and_3_out, and_4_out, and_5_out, not_1_out;
  wire [7:0] multiplexer_2_out, multiplexer_3_out;

  and and_1 (low_write_en_o, low_byte_i, str_data_i);
  and and_2 (high_write_en_o, high_byte_i, str_data_i);
  and and_3 (and_3_out, low_byte_i, high_byte_i);
  and and_4 (and_4_out, high_byte_i, ~low_byte_i);  // AND_Gate
  not not_1 (not_1_out, and_5_out);
  and and_5 (and_5_out, high_byte_i, low_byte_i);
  Multiplexer #(.width(8), .enable("false")) multiplexer_1 (
    .in0(wr_data_i[7:0]), .in1(wr_data_i[15:8]), .out(high_data_o), .sel(and_3_out));
  Multiplexer #(.width(8), .enable("false")) multiplexer_2 (
    .in0(rd_data_low_i), .in1(rd_data_high_i), .out(multiplexer_2_out), .sel(and_4_out));
  Multiplexer #(.width(8), .enable("false")) multiplexer_3 (
    .in0(rd_data_high_i), .in1({8{1'b0}}), .out(multiplexer_3_out), .sel(not_1_out));
  assign rd_data_o = ldr_data_i ? {multiplexer_3_out, multiplexer_2_out} : 16'bz;  // Controlled_Buffer controlled_buffer_1

  assign low_data_o = wr_data_i[7:0];

  // Other names for the same wires on the sheet: wr_data_high_o[7:0] = high_data_o;
  //   wr_data_low_o[7:0] = wr_data_i[7:0]

  // Notes on the sheet:
  //   Attention, votre version de Logisim
  //   ne contient pas de tracker. Si vous
  //   enregistrez votre projet, toutes les
  //   informations du tracker seront
  //   définitivement effacées.
  //   Write interface
  //   Read interface
endmodule

module processeur_ARO2 (
  input  [15:0] instr_data_i,
  input  [15:0] memory_rd_data_i,
  input  rst_i,
  input  clk_i,
  output [15:0] instr_addr_o,
  output [14:0] memory_addr_o,
  output [15:0] memory_wr_data_o,
  output memory_str_data_o,
  output memory_ldr_data,
  output memory_high_byte_o,
  output memory_low_byte_o
);

  wire is_unconditional_1_is_unconditional;
  wire [1:0] fetch_bus;
  wire [15:0] branch_addr, fetch_1_instr_data_o, fetch_1_pc_fut_o, offset_conditional_1_branch_address_o,
       offset_inconditional_1_branch_address_o, PC_pres;

  Register #(.width(16)) PC (.D(fetch_1_pc_fut_o), .en(1'b1), .clk(clk_i), .Q(PC_pres), .clr(rst_i));
  fetch fetch_1 (
    .fetch_en_i(1'b1), .instr_data_i(instr_data_i), .PC_pres_i(PC_pres), .branch_addr_i(branch_addr),
    .fetch_control_bus_i({1'b0, instr_data_i[11:8], fetch_bus}), .cpsr_i(4'b0000), .clk_i(clk_i),
    .rst_i(rst_i), .instr_addr_o(instr_addr_o), .instr_data_o(fetch_1_instr_data_o),
    .PC_fut_o(fetch_1_pc_fut_o));  // open: branch_o
  // Probe on fetch_1_instr_data_o
  is_conditional is_conditional_1 (.inst_addr_i(instr_data_i), .is_conditional(fetch_bus[1]));
  is_unconditional is_unconditional_1 (
    .inst_addr_i(instr_data_i), .is_unconditional(is_unconditional_1_is_unconditional));
  offset_inconditional offset_inconditional_1 (
    .instr_address_i(instr_data_i), .PC_pres_i(PC_pres),
    .branch_address_o(offset_inconditional_1_branch_address_o));
  offset_conditional offset_conditional_1 (
    .instr_add_i(instr_data_i), .PC_pres_i(PC_pres), .branch_address_o(offset_conditional_1_branch_address_o));
  or or_1 (fetch_bus[0], fetch_bus[1], is_unconditional_1_is_unconditional);
  Multiplexer #(.width(16), .enable("false")) multiplexer_1 (
    .in0(offset_inconditional_1_branch_address_o), .in1(offset_conditional_1_branch_address_o),
    .out(branch_addr), .sel(fetch_bus[1]));

  assign memory_addr_o = {15{1'b0}};
  assign memory_high_byte_o = 1'b0;
  assign memory_ldr_data = 1'b0;
  assign memory_low_byte_o = 1'b0;
  assign memory_str_data_o = 1'b0;
  assign memory_wr_data_o = {16{1'b0}};

  // Other names for the same wires on the sheet: clk_s = clk_i; is_conditional = fetch_bus[1];
  //   fetch_bus[5:2] = instr_data_i[11:8]; instr_data_s[15:0] = instr_data_i; instr_addr_s[15:0] = instr_addr_o;
  //   memory_rd_data_s[15:0] = memory_rd_data_i; rst_s = rst_i

  // Notes on the sheet:
  //   Attention, votre version de Logisim
  //   ne contient pas de tracker. Si vous
  //   enregistrez votre projet, toutes les
  //   informations du tracker seront
  //   définitivement effacées.
  //   Intruction memory inputs
  //   Memory interface inputs
  //   Standard inputs
  //   Processeur simplifié pour le cours ARO2
  //   Instruction memory outputs
  //   Memory interface outputs
endmodule

module fetch (
  input  fetch_en_i,
  input  [15:0] instr_data_i,
  input  [15:0] PC_pres_i,
  input  [15:0] branch_addr_i,
  input  [6:0] fetch_control_bus_i,
  input  [3:0] cpsr_i,
  input  clk_i,
  input  rst_i,
  output [15:0] instr_addr_o,
  output [15:0] instr_data_o,
  output [15:0] PC_fut_o,
  output branch_o
);

  wire and_1_out, condition_tester_1_cond_test_o;
  wire [15:0] adder_1_out, multiplexer_1_out;

  condition_tester condition_tester_1 (
    .cond_en_i(fetch_control_bus_i[1]), .cond_i(instr_data_i[11:8]), .Z_i(cpsr_i[0]), .C_i(cpsr_i[1]),
    .N_i(cpsr_i[2]), .V_i(cpsr_i[3]), .cond_test_o(condition_tester_1_cond_test_o));
  Adder #(.width(16)) adder_1 (.a(PC_pres_i), .b(16'h2), .out(adder_1_out));  // open: cin, cout
  and and_1 (and_1_out, condition_tester_1_cond_test_o, fetch_control_bus_i[0]);
  Multiplexer #(.width(16), .enable("false")) multiplexer_1 (
    .in0(adder_1_out), .in1(branch_addr_i), .out(multiplexer_1_out), .sel(and_1_out));
  Multiplexer #(.width(16), .enable("false")) multiplexer_2 (
    .in0(PC_pres_i), .in1(multiplexer_1_out), .out(PC_fut_o), .sel(fetch_en_i));

  assign branch_o = 1'b0;
  assign instr_addr_o = PC_pres_i;
  assign instr_data_o = instr_data_i;

  // Other names for the same wires on the sheet: branch_addr_s[15:0] = branch_addr_i; clk_s = clk_i;
  //   cpsr_s[3:0] = cpsr_i; fetch_control_bus_s[6:0] = fetch_control_bus_i; is_conditional = fetch_control_bus_i[1];
  //   fetch_en_s = fetch_en_i; instr_data_s[15:0] = instr_data_i; PC_fut_s[15:0] = PC_fut_o;
  //   PC_pres_s[15:0] = PC_pres_i; rst_s = rst_i

  // Notes on the sheet:
  //   Attention, votre version de Logisim
  //   ne contient pas de tracker. Si vous
  //   enregistrez votre projet, toutes les
  //   informations du tracker seront
  //   définitivement effacées.
  //   Entité FETCH
  //   L'instruction d'adressage me semble être la valeur futur de notre PC 
endmodule

module condition_tester (
  input  cond_en_i,
  input  [3:0] cond_i,
  input  Z_i,
  input  C_i,
  input  N_i,
  input  V_i,
  output cond_test_o
);

  wire and_1_out, and_2_out, comparator_1_eq, not_1_out, not_2_out, not_3_out, not_4_out, not_5_out,
       not_6_out, not_7_out, not_8_out, or_1_out, or_2_out;
  wire [3:0] multiplexer_1_out;

  and and_1 (and_1_out, C_i, not_1_out);
  not not_1 (not_1_out, Z_i);
  not not_2 (not_2_out, C_i);
  or or_1 (or_1_out, not_2_out, Z_i);
  Comparator #(.width(1), .mode("unsigned")) comparator_1 (.a(N_i), .b(V_i), .eq(comparator_1_eq));  // open: gt, lt
  not not_3 (not_3_out, Z_i);
  not not_4 (not_4_out, comparator_1_eq);
  and and_2 (and_2_out, comparator_1_eq, not_3_out);
  or or_2 (or_2_out, not_4_out, Z_i);
  not not_5 (not_5_out, Z_i);
  not not_6 (not_6_out, C_i);
  not not_7 (not_7_out, N_i);
  not not_8 (not_8_out, V_i);
  Multiplexer #(.width(4), .enable("false")) multiplexer_1 (
    .in0(4'b1110), .in1(cond_i), .out(multiplexer_1_out), .sel(cond_en_i));
  Multiplexer #(.select(4), .enable("false")) multiplexer_2 (
    .in0(Z_i), .in1(not_5_out), .in2(C_i), .in3(not_6_out), .in4(N_i), .in5(not_7_out), .in6(V_i),
    .in7(not_8_out), .in8(and_1_out), .in9(or_1_out), .in10(comparator_1_eq), .in11(not_4_out),
    .in12(and_2_out), .in13(or_2_out), .in14(1'b1), .in15(1'b1), .out(cond_test_o), .sel(multiplexer_1_out));

  // Notes on the sheet:
  //   Attention, votre version de Logisim
  //   ne contient pas de tracker. Si vous
  //   enregistrez votre projet, toutes les
  //   informations du tracker seront
  //   définitivement effacées.
  //   Always (Inconditionnel)
endmodule

module decode (
  input  decode_en_i,
  input  [15:0] instr_data_i,
  input  rst_i,
  input  clk_i,
  output [2:0] adr_reg_d_o,
  output [2:0] adr_reg_n_o,
  output [2:0] adr_reg_m_o,
  output [2:0] adr_reg_mem_o,
  output [2:0] imm3_o,
  output [4:0] imm5_o,
  output [10:0] offset11_o,
  output [7:0] offset8_o,
  output [7:0] imm8_o,
  output [1:0] reg_bank_control_bus_o,
  output [14:0] execute_control_bus_o,
  output [4:0] mem_control_bus_o,
  output [6:0] fetch_control_bus_o,
  output link_en_o,
  output RAW_detected
);

  decode_instr_splitter Instr_Splitter_Inst ();  // open: instr_i, rd_2_0_o, rd_10_8_o, rn_5_3_o, rm_8_6_o, offset3_8_6_o, offset5_10_6_o, offset8_7_0_o, offset11_10_0_o, cond_11_8_o
  main_control_unit Control_Unit_Inst ();  // open: decode_en_i, instr_i, cond_i, raw_detected_i, rst_i, clk_i, fetch_control_bus_o, decode_control_bus_o, reg_bank_control_bus_o, execute_control_bus_o, mem_control_bus_o, use_rd_o, use_rn_o, use_rm_o, use_rmem_o

  assign adr_reg_d_o = 3'b000;
  assign adr_reg_m_o = 3'b000;
  assign adr_reg_mem_o = 3'b000;
  assign adr_reg_n_o = 3'b000;
  assign execute_control_bus_o = {15{1'b0}};
  assign fetch_control_bus_o = {7{1'b0}};
  assign imm3_o = 3'b000;
  assign imm5_o = {5{1'b0}};
  assign imm8_o = {8{1'b0}};
  assign link_en_o = 1'b0;
  assign mem_control_bus_o = {5{1'b0}};
  assign offset8_o = {8{1'b0}};
  assign offset11_o = {11{1'b0}};
  assign RAW_detected = 1'b0;
  assign reg_bank_control_bus_o = 2'b00;

  // Other names for the same wires on the sheet: clk_s = clk_i; decode_en_s = decode_en_i;
  //   instr_data_s[15:0] = instr_data_i; rst_s = rst_i

  // Notes on the sheet:
  //   Attention, votre version de Logisim
  //   ne contient pas de tracker. Si vous
  //   enregistrez votre projet, toutes les
  //   informations du tracker seront
  //   définitivement effacées.
  //   Entité DECODE
endmodule

module decode_instr_splitter (
  input  [15:0] instr_i,
  output [2:0] rd_2_0_o,
  output [2:0] rd_10_8_o,
  output [2:0] rn_5_3_o,
  output [2:0] rm_8_6_o,
  output [2:0] offset3_8_6_o,
  output [4:0] offset5_10_6_o,
  output [7:0] offset8_7_0_o,
  output [10:0] offset11_10_0_o,
  output [3:0] cond_11_8_o
);


  assign cond_11_8_o = instr_i[11:8];
  assign offset3_8_6_o = instr_i[8:6];
  assign offset5_10_6_o = instr_i[10:6];
  assign offset8_7_0_o = instr_i[7:0];
  assign offset11_10_0_o = instr_i[10:0];
  assign rd_2_0_o = instr_i[2:0];
  assign rd_10_8_o = instr_i[10:8];
  assign rm_8_6_o = instr_i[8:6];
  assign rn_5_3_o = instr_i[5:3];

  // Notes on the sheet:
  //   Attention, votre version de Logisim
  //   ne contient pas de tracker. Si vous
  //   enregistrez votre projet, toutes les
  //   informations du tracker seront
  //   définitivement effacées.
endmodule

module main_control_unit (
  input  decode_en_i,
  input  [15:0] instr_i,
  input  [3:0] cond_i,
  input  raw_detected_i,
  input  rst_i,
  input  clk_i,
  output [6:0] fetch_control_bus_o,
  output [5:0] decode_control_bus_o,
  output [1:0] reg_bank_control_bus_o,
  output [14:0] execute_control_bus_o,
  output [4:0] mem_control_bus_o,
  output use_rd_o,
  output use_rn_o,
  output use_rm_o,
  output use_rmem_o
);

  wire add_r_imm_s, add_r_r_imm_s, add_r_r_r_s, and_r_r_s, asr_r_r_imm_s, asr_r_r_s, b_cond_s, b_incond_s,
       bl_lsb_s, bl_msb_s, byte_s, cond_en_s, eor_r_r_s, ldr_data_s, ldrb_r_r_imm_s, ldrb_r_r_r_s,
       ldrh_r_r_imm_s, ldrh_r_r_r_s, link_en_s, lsl_r_r_imm_s, lsl_r_r_s, lsr_r_r_imm_s, lsr_r_r_s,
       mov_r_imm_s, mvn_r_r_s, neg_r_r_s, orr_r_r_s, reg_bank_wr_s, ror_r_r_s, sel_cpsr_s, sel_mem_s,
       sel_operand_1_s, sel_PC_s, sel_rd_s, sel_rm_s, sel_shift_s, str_data_s, strb_r_r_imm_s, strb_r_r_r_s,
       strh_r_r_imm_s, strh_r_r_r_s, sub_r_imm_s, sub_r_r_imm_s, sub_r_r_r_s;
  wire [1:0] sel_operand_2_s, sel_rn_s;
  wire [2:0] sel_mult_2_s, sel_op_alu_s, sel_op_shift_s;

  opcode_supported_unit opcode_supported_unit_1 (
    .instr_i(instr_i), .lsl_r_r_imm_o(lsl_r_r_imm_s), .lsr_r_r_imm_o(lsr_r_r_imm_s),
    .asr_r_r_imm_o(asr_r_r_imm_s), .add_r_r_r_o(add_r_r_r_s), .add_r_r_imm_o(add_r_r_imm_s),
    .sub_r_r_r_o(sub_r_r_r_s), .sub_r_r_imm_o(sub_r_r_imm_s), .mov_r_imm_o(mov_r_imm_s),
    .add_r_imm_o(add_r_imm_s), .sub_r_imm_o(sub_r_imm_s), .and_r_r_o(and_r_r_s), .eor_r_r_o(eor_r_r_s),
    .lsl_r_r_o(lsl_r_r_s), .lsr_r_r_o(lsr_r_r_s), .asr_r_r_o(asr_r_r_s), .ror_r_r_o(ror_r_r_s),
    .neg_r_r_o(neg_r_r_s), .orr_r_r_o(orr_r_r_s), .mvn_r_r_o(mvn_r_r_s), .strb_r_r_r_o(strb_r_r_r_s),
    .ldrb_r_r_r_o(ldrb_r_r_r_s), .strh_r_r_r_o(strh_r_r_r_s), .ldrh_r_r_r_o(ldrh_r_r_r_s),
    .strb_r_r_imm_o(strb_r_r_imm_s), .ldrb_r_r_imm_o(ldrb_r_r_imm_s), .strh_r_r_imm_o(strh_r_r_imm_s),
    .ldrh_r_r_imm_o(ldrh_r_r_imm_s), .b_cond_o(b_cond_s), .b_incond_o(b_incond_s), .bl_msb_o(bl_msb_s),
    .bl_lsb_o(bl_lsb_s));
  fetch_control_unit fetch (
    .instr_i({1'b0, bl_lsb_s, bl_msb_s, b_incond_s, b_cond_s, ldrh_r_r_imm_s, strh_r_r_imm_s, ldrb_r_r_imm_s, strb_r_r_imm_s, ldrh_r_r_r_s, strh_r_r_r_s, ldrb_r_r_r_s, strb_r_r_r_s, mvn_r_r_s, orr_r_r_s, neg_r_r_s, ror_r_r_s, asr_r_r_s, lsr_r_r_s, lsl_r_r_s, eor_r_r_s, and_r_r_s, sub_r_imm_s, add_r_imm_s, mov_r_imm_s, sub_r_r_imm_s, sub_r_r_r_s, add_r_r_imm_s, add_r_r_r_s, asr_r_r_imm_s, lsr_r_r_imm_s, lsl_r_r_imm_s}),
    .sel_cpsr_o(sel_cpsr_s), .link_en_o(link_en_s), .sel_PC_o(sel_PC_s), .cond_en_o(cond_en_s));
  decode_control_unit decode (
    .instr_i({1'b0, bl_lsb_s, bl_msb_s, b_incond_s, b_cond_s, ldrh_r_r_imm_s, strh_r_r_imm_s, ldrb_r_r_imm_s, strb_r_r_imm_s, ldrh_r_r_r_s, strh_r_r_r_s, ldrb_r_r_r_s, strb_r_r_r_s, mvn_r_r_s, orr_r_r_s, neg_r_r_s, ror_r_r_s, asr_r_r_s, lsr_r_r_s, lsl_r_r_s, eor_r_r_s, and_r_r_s, sub_r_imm_s, add_r_imm_s, mov_r_imm_s, sub_r_r_imm_s, sub_r_r_r_s, add_r_r_imm_s, add_r_r_r_s, asr_r_r_imm_s, lsr_r_r_imm_s, lsl_r_r_imm_s}),
    .sel_rn_o(sel_rn_s), .sel_rm_o(sel_rm_s), .sel_rd_o(sel_rd_s), .use_rd_o(use_rd_o), .use_rn_o(use_rn_o),
    .use_rm_o(use_rm_o), .use_rmem_o(use_rmem_o));
  reg_bank_control_unit reg_bank (
    .instr_i({1'b0, bl_lsb_s, bl_msb_s, b_incond_s, b_cond_s, ldrh_r_r_imm_s, strh_r_r_imm_s, ldrb_r_r_imm_s, strb_r_r_imm_s, ldrh_r_r_r_s, strh_r_r_r_s, ldrb_r_r_r_s, strb_r_r_r_s, mvn_r_r_s, orr_r_r_s, neg_r_r_s, ror_r_r_s, asr_r_r_s, lsr_r_r_s, lsl_r_r_s, eor_r_r_s, and_r_r_s, sub_r_imm_s, add_r_imm_s, mov_r_imm_s, sub_r_r_imm_s, sub_r_r_r_s, add_r_r_imm_s, add_r_r_r_s, asr_r_r_imm_s, lsr_r_r_imm_s, lsl_r_r_imm_s}),
    .reg_bank_wr_o(reg_bank_wr_s));
  execute_control_unit execute (
    .instr_i({1'b0, bl_lsb_s, bl_msb_s, b_incond_s, b_cond_s, ldrh_r_r_imm_s, strh_r_r_imm_s, ldrb_r_r_imm_s, strb_r_r_imm_s, ldrh_r_r_r_s, strh_r_r_r_s, ldrb_r_r_r_s, strb_r_r_r_s, mvn_r_r_s, orr_r_r_s, neg_r_r_s, ror_r_r_s, asr_r_r_s, lsr_r_r_s, lsl_r_r_s, eor_r_r_s, and_r_r_s, sub_r_imm_s, add_r_imm_s, mov_r_imm_s, sub_r_r_imm_s, sub_r_r_r_s, add_r_r_imm_s, add_r_r_r_s, asr_r_r_imm_s, lsr_r_r_imm_s, lsl_r_r_imm_s}),
    .sel_operand_1_o(sel_operand_1_s), .sel_operand_2_o(sel_operand_2_s), .sel_op_shift_o(sel_op_shift_s),
    .sel_op_alu_o(sel_op_alu_s), .sel_mult_2_o(sel_mult_2_s), .sel_shift_o(sel_shift_s));
  memory_access_control_unit memory_acces (
    .instr_i({1'b0, bl_lsb_s, bl_msb_s, b_incond_s, b_cond_s, ldrh_r_r_imm_s, strh_r_r_imm_s, ldrb_r_r_imm_s, strb_r_r_imm_s, ldrh_r_r_r_s, strh_r_r_r_s, ldrb_r_r_r_s, strb_r_r_r_s, mvn_r_r_s, orr_r_r_s, neg_r_r_s, ror_r_r_s, asr_r_r_s, lsr_r_r_s, lsl_r_r_s, eor_r_r_s, and_r_r_s, sub_r_imm_s, add_r_imm_s, mov_r_imm_s, sub_r_r_imm_s, sub_r_r_r_s, add_r_r_imm_s, add_r_r_r_s, asr_r_r_imm_s, lsr_r_r_imm_s, lsl_r_r_imm_s}),
    .sel_mem_o(sel_mem_s), .str_data_o(str_data_s), .ldr_data_o(ldr_data_s), .byte_o(byte_s));
  bus_constructor bus_constructor_1 (
    .fetch_en_i(1'b0), .decode_en_i(1'b0), .reg_bank_en_i(1'b0), .execute_en_i(1'b0),
    .memory_access_en_i(1'b0), .cond_i(cond_i), .sel_cpsr_i(sel_cpsr_s), .link_en_i(link_en_s),
    .sel_PC_i(sel_PC_s), .cond_en_i(cond_en_s), .sel_rn_i(sel_rn_s), .sel_rm_i(sel_rm_s),
    .sel_rd_i(sel_rd_s), .reg_bank_wr_i(reg_bank_wr_s), .sel_operand_1_i(sel_operand_1_s),
    .sel_operand_2_i(sel_operand_2_s), .sel_op_shift_i(sel_op_shift_s), .sel_op_alu_i(sel_op_alu_s),
    .sel_mult_2_i(sel_mult_2_s), .sel_shift_i(sel_shift_s), .sel_mem_i(sel_mem_s), .str_data_i(str_data_s),
    .ldr_data_i(ldr_data_s), .byte_i(byte_s), .fetch_control_bus_o(fetch_control_bus_o),
    .decode_control_bus_o(decode_control_bus_o), .reg_bank_control_bus_o(reg_bank_control_bus_o),
    .execute_control_bus_o(execute_control_bus_o), .mem_control_bus_o(mem_control_bus_o));

  // Other names for the same wires on the sheet: clk_s = clk_i; cond_s[3:0] = cond_i;
  //   decode_control_bus_s[5:0] = decode_control_bus_o; decode_en_s = decode_en_i;
  //   execute_control_bus_s[14:0] = execute_control_bus_o; fetch_control_bus_s[6:0] = fetch_control_bus_o;
  //   mem_control_bus_s[4:0] = mem_control_bus_o; RAW = raw_detected_i;
  //   reg_bank_control_bus_s[1:0] = reg_bank_control_bus_o; rst_s = rst_i; use_rd_s = use_rd_o; use_rm_s = use_rm_o;
  //   use_rmem_s = use_rmem_o; use_rn_s = use_rn_o

  // Notes on the sheet:
  //   Attention, votre version de Logisim
  //   ne contient pas de tracker. Si vous
  //   enregistrez votre projet, toutes les
  //   informations du tracker seront
  //   définitivement effacées.
endmodule

module opcode_supported_unit (
  input  [15:0] instr_i,
  output lsl_r_r_imm_o,
  output lsr_r_r_imm_o,
  output asr_r_r_imm_o,
  output add_r_r_r_o,
  output add_r_r_imm_o,
  output sub_r_r_r_o,
  output sub_r_r_imm_o,
  output mov_r_imm_o,
  output add_r_imm_o,
  output sub_r_imm_o,
  output and_r_r_o,
  output eor_r_r_o,
  output lsl_r_r_o,
  output lsr_r_r_o,
  output asr_r_r_o,
  output ror_r_r_o,
  output neg_r_r_o,
  output orr_r_r_o,
  output mvn_r_r_o,
  output strb_r_r_r_o,
  output ldrb_r_r_r_o,
  output strh_r_r_r_o,
  output ldrh_r_r_r_o,
  output strb_r_r_imm_o,
  output ldrb_r_r_imm_o,
  output strh_r_r_imm_o,
  output ldrh_r_r_imm_o,
  output b_cond_o,
  output b_incond_o,
  output bl_msb_o,
  output bl_lsb_o
);

  wire comparator_20_eq, comparator_21_eq;

  Comparator #(.width(5), .mode("unsigned")) comparator_1 (
    .a(instr_i[15:11]), .b({5{1'b0}}), .eq(lsl_r_r_imm_o));  // open: gt, lt
  Comparator #(.width(5), .mode("unsigned")) comparator_2 (
    .a(instr_i[15:11]), .b(5'b00001), .eq(lsr_r_r_imm_o));  // open: gt, lt
  Comparator #(.width(5), .mode("unsigned")) comparator_3 (
    .a(instr_i[15:11]), .b(5'b00010), .eq(asr_r_r_imm_o));  // open: gt, lt
  Comparator #(.width(7), .mode("unsigned")) comparator_4 (
    .a(instr_i[15:9]), .b(7'b0001100), .eq(add_r_r_r_o));  // open: gt, lt
  Comparator #(.width(7), .mode("unsigned")) comparator_5 (
    .a(instr_i[15:9]), .b(7'b0001110), .eq(add_r_r_imm_o));  // open: gt, lt
  Comparator #(.width(7), .mode("unsigned")) comparator_6 (
    .a(instr_i[15:9]), .b(7'b0001101), .eq(sub_r_r_r_o));  // open: gt, lt
  Comparator #(.width(7), .mode("unsigned")) comparator_7 (
    .a(instr_i[15:9]), .b(7'b0001111), .eq(sub_r_r_imm_o));  // open: gt, lt
  Comparator #(.width(5), .mode("unsigned")) comparator_8 (
    .a(instr_i[15:11]), .b(5'b00100), .eq(mov_r_imm_o));  // open: gt, lt
  Comparator #(.width(5), .mode("unsigned")) comparator_9 (
    .a(instr_i[15:11]), .b(5'b00110), .eq(add_r_imm_o));  // open: gt, lt
  Comparator #(.width(5), .mode("unsigned")) comparator_10 (
    .a(instr_i[15:11]), .b(5'b00111), .eq(sub_r_imm_o));  // open: gt, lt
  Comparator #(.width(10), .mode("unsigned")) comparator_11 (
    .a(instr_i[15:6]), .b(10'h100), .eq(and_r_r_o));  // open: gt, lt
  Comparator #(.width(10), .mode("unsigned")) comparator_12 (
    .a(instr_i[15:6]), .b(10'h101), .eq(eor_r_r_o));  // open: gt, lt
  Comparator #(.width(10), .mode("unsigned")) comparator_13 (
    .a(instr_i[15:6]), .b(10'h102), .eq(lsl_r_r_o));  // open: gt, lt
  Comparator #(.width(10), .mode("unsigned")) comparator_14 (
    .a(instr_i[15:6]), .b(10'h103), .eq(lsr_r_r_o));  // open: gt, lt
  Comparator #(.width(10), .mode("unsigned")) comparator_15 (
    .a(instr_i[15:6]), .b(10'h104), .eq(asr_r_r_o));  // open: gt, lt
  Comparator #(.width(10), .mode("unsigned")) comparator_16 (
    .a(instr_i[15:6]), .b(10'h107), .eq(ror_r_r_o));  // open: gt, lt
  Comparator #(.width(10), .mode("unsigned")) comparator_17 (
    .a(instr_i[15:6]), .b(10'h109), .eq(neg_r_r_o));  // open: gt, lt
  Comparator #(.width(10), .mode("unsigned")) comparator_18 (
    .a(instr_i[15:6]), .b(10'h10c), .eq(orr_r_r_o));  // open: gt, lt
  Comparator #(.width(10), .mode("unsigned")) comparator_19 (
    .a(instr_i[15:6]), .b(10'h10f), .eq(mvn_r_r_o));  // open: gt, lt
  Comparator #(.width(4), .mode("unsigned")) comparator_20 (
    .a(instr_i[15:12]), .b(4'b1101), .eq(comparator_20_eq));  // open: gt, lt
  Comparator #(.width(4), .mode("unsigned")) comparator_21 (
    .a(instr_i[11:8]), .b(4'b1111), .eq(comparator_21_eq));  // open: gt, lt
  Comparator #(.width(5), .mode("unsigned")) comparator_22 (
    .a(instr_i[15:11]), .b(5'b11100), .eq(b_incond_o));  // open: gt, lt
  Comparator #(.width(5), .mode("unsigned")) comparator_23 (
    .a(instr_i[15:11]), .b(5'b11110), .eq(bl_msb_o));  // open: gt, lt
  Comparator #(.width(5), .mode("unsigned")) comparator_24 (
    .a(instr_i[15:11]), .b({5{1'b1}}), .eq(bl_lsb_o));  // open: gt, lt
  and and_1 (b_cond_o, comparator_20_eq, ~comparator_21_eq);  // AND_Gate

  assign ldrb_r_r_imm_o = 1'b0;
  assign ldrb_r_r_r_o = 1'b0;
  assign ldrh_r_r_imm_o = 1'b0;
  assign ldrh_r_r_r_o = 1'b0;
  assign strb_r_r_imm_o = 1'b0;
  assign strb_r_r_r_o = 1'b0;
  assign strh_r_r_imm_o = 1'b0;
  assign strh_r_r_r_o = 1'b0;

  // Other names for the same wires on the sheet: add_r_imm = add_r_imm_o; add_r_r_imm = add_r_r_imm_o;
  //   add_r_r_r = add_r_r_r_o; and_r_r = and_r_r_o; asr_r_r = asr_r_r_o; asr_r_r_imm = asr_r_r_imm_o;
  //   b_cond = b_cond_o; b_incond = b_incond_o; bl_lsb = bl_lsb_o; bl_msb = bl_msb_o; eor_r_r = eor_r_r_o;
  //   lsl_r_r = lsl_r_r_o; lsl_r_r_imm = lsl_r_r_imm_o; lsr_r_r = lsr_r_r_o; lsr_r_r_imm = lsr_r_r_imm_o;
  //   mov_r_imm = mov_r_imm_o; mvn_r_r = mvn_r_r_o; neg_r_r = neg_r_r_o; orr_r_r = orr_r_r_o; ror_r_r = ror_r_r_o;
  //   sub_r_imm = sub_r_imm_o; sub_r_r_imm = sub_r_r_imm_o; sub_r_r_r = sub_r_r_r_o

  // Notes on the sheet:
  //   Attention, votre version de Logisim
  //   ne contient pas de tracker. Si vous
  //   enregistrez votre projet, toutes les
  //   informations du tracker seront
  //   définitivement effacées.
  //   Extraction des instructions supportées
endmodule

module fetch_control_unit (
  input  [31:0] instr_i,
  output sel_cpsr_o,
  output link_en_o,
  output sel_PC_o,
  output cond_en_o
);


  assign cond_en_o = 1'b0;
  assign link_en_o = 1'b0;
  assign sel_cpsr_o = 1'b0;
  assign sel_PC_o = 1'b0;

  // Other names for the same wires on the sheet: lsl_r_r_imm_s = instr_i[0]; lsr_r_r_imm_s = instr_i[1];
  //   asr_r_r_imm_s = instr_i[2]; add_r_r_r_s = instr_i[3]; add_r_r_imm_s = instr_i[4]; sub_r_r_r_s = instr_i[5];
  //   sub_r_r_imm_s = instr_i[6]; mov_r_imm_s = instr_i[7]; add_r_imm_s = instr_i[8]; sub_r_imm_s = instr_i[9];
  //   and_r_r_s = instr_i[10]; eor_r_r_s = instr_i[11]; lsl_r_r_s = instr_i[12]; lsr_r_r_s = instr_i[13];
  //   asr_r_r_s = instr_i[14]; ror_r_r_s = instr_i[15]; neg_r_r_s = instr_i[16]; orr_r_r_s = instr_i[17];
  //   mvn_r_r_s = instr_i[18]; strb_r_r_r_s = instr_i[19]; ldrb_r_r_r_s = instr_i[20]; strh_r_r_r_s = instr_i[21];
  //   ldrh_r_r_r_s = instr_i[22]; strb_r_r_imm_s = instr_i[23]; ldrb_r_r_imm_s = instr_i[24];
  //   strh_r_r_imm_s = instr_i[25]; ldrh_r_r_imm_s = instr_i[26]; b_cond_s = instr_i[27]; b_incond_s = instr_i[28];
  //   bl_msb_s = instr_i[29]; bl_lsb_s = instr_i[30]

  // Notes on the sheet:
  //   Attention, votre version de Logisim
  //   ne contient pas de tracker. Si vous
  //   enregistrez votre projet, toutes les
  //   informations du tracker seront
  //   définitivement effacées.
endmodule

module decode_control_unit (
  input  [31:0] instr_i,
  output [1:0] sel_rn_o,
  output sel_rm_o,
  output sel_rd_o,
  output use_rd_o,
  output use_rn_o,
  output use_rm_o,
  output use_rmem_o
);


  assign sel_rd_o = 1'b0;
  assign sel_rm_o = 1'b0;
  assign sel_rn_o = 2'b00;
  assign use_rd_o = 1'b0;
  assign use_rm_o = 1'b0;
  assign use_rmem_o = 1'b0;
  assign use_rn_o = 1'b0;

  // Other names for the same wires on the sheet: lsl_r_r_imm_s = instr_i[0]; lsr_r_r_imm_s = instr_i[1];
  //   asr_r_r_imm_s = instr_i[2]; add_r_r_r_s = instr_i[3]; add_r_r_imm_s = instr_i[4]; sub_r_r_r_s = instr_i[5];
  //   sub_r_r_imm_s = instr_i[6]; mov_r_imm_s = instr_i[7]; add_r_imm_s = instr_i[8]; sub_r_imm_s = instr_i[9];
  //   and_r_r_s = instr_i[10]; eor_r_r_s = instr_i[11]; lsl_r_r_s = instr_i[12]; lsr_r_r_s = instr_i[13];
  //   asr_r_r_s = instr_i[14]; ror_r_r_s = instr_i[15]; neg_r_r_s = instr_i[16]; orr_r_r_s = instr_i[17];
  //   mvn_r_r_s = instr_i[18]; strb_r_r_r_s = instr_i[19]; ldrb_r_r_r_s = instr_i[20]; strh_r_r_r_s = instr_i[21];
  //   ldrh_r_r_r_s = instr_i[22]; strb_r_r_imm_s = instr_i[23]; ldrb_r_r_imm_s = instr_i[24];
  //   strh_r_r_imm_s = instr_i[25]; ldrh_r_r_imm_s = instr_i[26]; b_cond_s = instr_i[27]; b_incond_s = instr_i[28];
  //   bl_msb_s = instr_i[29]; bl_lsb_s = instr_i[30]

  // Notes on the sheet:
  //   Attention, votre version de Logisim
  //   ne contient pas de tracker. Si vous
  //   enregistrez votre projet, toutes les
  //   informations du tracker seront
  //   définitivement effacées.
endmodule

module reg_bank_control_unit (
  input  [31:0] instr_i,
  output reg_bank_wr_o
);


  assign reg_bank_wr_o = 1'b0;

  // Other names for the same wires on the sheet: lsl_r_r_imm_s = instr_i[0]; lsr_r_r_imm_s = instr_i[1];
  //   asr_r_r_imm_s = instr_i[2]; add_r_r_r_s = instr_i[3]; add_r_r_imm_s = instr_i[4]; sub_r_r_r_s = instr_i[5];
  //   sub_r_r_imm_s = instr_i[6]; mov_r_imm_s = instr_i[7]; add_r_imm_s = instr_i[8]; sub_r_imm_s = instr_i[9];
  //   and_r_r_s = instr_i[10]; eor_r_r_s = instr_i[11]; lsl_r_r_s = instr_i[12]; lsr_r_r_s = instr_i[13];
  //   asr_r_r_s = instr_i[14]; ror_r_r_s = instr_i[15]; neg_r_r_s = instr_i[16]; orr_r_r_s = instr_i[17];
  //   mvn_r_r_s = instr_i[18]; strb_r_r_r_s = instr_i[19]; ldrb_r_r_r_s = instr_i[20]; strh_r_r_r_s = instr_i[21];
  //   ldrh_r_r_r_s = instr_i[22]; strb_r_r_imm_s = instr_i[23]; ldrb_r_r_imm_s = instr_i[24];
  //   strh_r_r_imm_s = instr_i[25]; ldrh_r_r_imm_s = instr_i[26]; b_cond_s = instr_i[27]; b_incond_s = instr_i[28];
  //   bl_msb_s = instr_i[29]; bl_lsb_s = instr_i[30]

  // Notes on the sheet:
  //   Attention, votre version de Logisim
  //   ne contient pas de tracker. Si vous
  //   enregistrez votre projet, toutes les
  //   informations du tracker seront
  //   définitivement effacées.
endmodule

module execute_control_unit (
  input  [31:0] instr_i,
  output sel_operand_1_o,
  output [1:0] sel_operand_2_o,
  output [2:0] sel_op_shift_o,
  output [2:0] sel_op_alu_o,
  output [2:0] sel_mult_2_o,
  output sel_shift_o
);


  assign sel_mult_2_o = 3'b000;
  assign sel_op_alu_o = 3'b000;
  assign sel_op_shift_o = 3'b000;
  assign sel_operand_1_o = 1'b0;
  assign sel_operand_2_o = 2'b00;
  assign sel_shift_o = 1'b0;

  // Other names for the same wires on the sheet: lsl_r_r_imm_s = instr_i[0]; lsr_r_r_imm_s = instr_i[1];
  //   asr_r_r_imm_s = instr_i[2]; add_r_r_r_s = instr_i[3]; add_r_r_imm_s = instr_i[4]; sub_r_r_r_s = instr_i[5];
  //   sub_r_r_imm_s = instr_i[6]; mov_r_imm_s = instr_i[7]; add_r_imm_s = instr_i[8]; sub_r_imm_s = instr_i[9];
  //   and_r_r_s = instr_i[10]; eor_r_r_s = instr_i[11]; lsl_r_r_s = instr_i[12]; lsr_r_r_s = instr_i[13];
  //   asr_r_r_s = instr_i[14]; ror_r_r_s = instr_i[15]; neg_r_r_s = instr_i[16]; orr_r_r_s = instr_i[17];
  //   mvn_r_r_s = instr_i[18]; strb_r_r_r_s = instr_i[19]; ldrb_r_r_r_s = instr_i[20]; strh_r_r_r_s = instr_i[21];
  //   ldrh_r_r_r_s = instr_i[22]; strb_r_r_imm_s = instr_i[23]; ldrb_r_r_imm_s = instr_i[24];
  //   strh_r_r_imm_s = instr_i[25]; ldrh_r_r_imm_s = instr_i[26]; b_cond_s = instr_i[27]; b_incond_s = instr_i[28];
  //   bl_msb_s = instr_i[29]; bl_lsb_s = instr_i[30]

  // Notes on the sheet:
  //   Attention, votre version de Logisim
  //   ne contient pas de tracker. Si vous
  //   enregistrez votre projet, toutes les
  //   informations du tracker seront
  //   définitivement effacées.
endmodule

module memory_access_control_unit (
  input  [31:0] instr_i,
  output sel_mem_o,
  output str_data_o,
  output ldr_data_o,
  output byte_o
);


  assign byte_o = 1'b0;
  assign ldr_data_o = 1'b0;
  assign sel_mem_o = 1'b0;
  assign str_data_o = 1'b0;

  // Other names for the same wires on the sheet: lsl_r_r_imm_s = instr_i[0]; lsr_r_r_imm_s = instr_i[1];
  //   asr_r_r_imm_s = instr_i[2]; add_r_r_r_s = instr_i[3]; add_r_r_imm_s = instr_i[4]; sub_r_r_r_s = instr_i[5];
  //   sub_r_r_imm_s = instr_i[6]; mov_r_imm_s = instr_i[7]; add_r_imm_s = instr_i[8]; sub_r_imm_s = instr_i[9];
  //   and_r_r_s = instr_i[10]; eor_r_r_s = instr_i[11]; lsl_r_r_s = instr_i[12]; lsr_r_r_s = instr_i[13];
  //   asr_r_r_s = instr_i[14]; ror_r_r_s = instr_i[15]; neg_r_r_s = instr_i[16]; orr_r_r_s = instr_i[17];
  //   mvn_r_r_s = instr_i[18]; strb_r_r_r_s = instr_i[19]; ldrb_r_r_r_s = instr_i[20]; strh_r_r_r_s = instr_i[21];
  //   ldrh_r_r_r_s = instr_i[22]; strb_r_r_imm_s = instr_i[23]; ldrb_r_r_imm_s = instr_i[24];
  //   strh_r_r_imm_s = instr_i[25]; ldrh_r_r_imm_s = instr_i[26]; b_cond_s = instr_i[27]; b_incond_s = instr_i[28];
  //   bl_msb_s = instr_i[29]; bl_lsb_s = instr_i[30]

  // Notes on the sheet:
  //   Attention, votre version de Logisim
  //   ne contient pas de tracker. Si vous
  //   enregistrez votre projet, toutes les
  //   informations du tracker seront
  //   définitivement effacées.
endmodule

module bus_constructor (
  input  fetch_en_i,
  input  decode_en_i,
  input  reg_bank_en_i,
  input  execute_en_i,
  input  memory_access_en_i,
  input  [3:0] cond_i,
  input  sel_cpsr_i,
  input  link_en_i,
  input  sel_PC_i,
  input  cond_en_i,
  input  [1:0] sel_rn_i,
  input  sel_rm_i,
  input  sel_rd_i,
  input  reg_bank_wr_i,
  input  sel_operand_1_i,
  input  [1:0] sel_operand_2_i,
  input  [2:0] sel_op_shift_i,
  input  [2:0] sel_op_alu_i,
  input  [2:0] sel_mult_2_i,
  input  sel_shift_i,
  input  sel_mem_i,
  input  str_data_i,
  input  ldr_data_i,
  input  byte_i,
  output [6:0] fetch_control_bus_o,
  output [5:0] decode_control_bus_o,
  output [1:0] reg_bank_control_bus_o,
  output [14:0] execute_control_bus_o,
  output [4:0] mem_control_bus_o
);


  assign decode_control_bus_o = {decode_en_i, sel_rd_i, link_en_i, sel_rm_i, sel_rn_i};
  assign execute_control_bus_o = {execute_en_i, sel_mult_2_i, sel_cpsr_i, sel_shift_i, sel_operand_1_i, sel_operand_2_i, sel_op_alu_i, sel_op_shift_i};
  assign fetch_control_bus_o = {fetch_en_i, cond_i, cond_en_i, sel_PC_i};
  assign mem_control_bus_o = {memory_access_en_i, byte_i, ldr_data_i, str_data_i, sel_mem_i};
  assign reg_bank_control_bus_o = {reg_bank_wr_i, reg_bank_en_i};

  // Other names for the same wires on the sheet: decode_control_bus_s[5:0] = {decode_en_i, sel_rd_i, link_en_i, sel_rm_i, sel_rn_i};
  //   sel_rn_s[1:0] = sel_rn_i; sel_rm_s = sel_rm_i; link_en_s = link_en_i; sel_rd_s = sel_rd_i;
  //   decode_en_s = decode_en_i;
  //   execute_control_bus_s[14:0] = {execute_en_i, sel_mult_2_i, sel_cpsr_i, sel_shift_i, sel_operand_1_i, sel_operand_2_i, sel_op_alu_i, sel_op_shift_i};
  //   sel_op_shift_s[2:0] = sel_op_shift_i; sel_op_alu_s[2:0] = sel_op_alu_i; sel_operand_2_s[1:0] = sel_operand_2_i;
  //   sel_operand_1_s = sel_operand_1_i; sel_shift_s = sel_shift_i; sel_cpsr_s = sel_cpsr_i;
  //   sel_mult_2_s[2:0] = sel_mult_2_i; execute_en_s = execute_en_i;
  //   fetch_control_bus_s[6:0] = {fetch_en_i, cond_i, cond_en_i, sel_PC_i}; sel_PC_s = sel_PC_i;
  //   cond_en_s = cond_en_i; cond_s[3:0] = cond_i; fetch_en_s = fetch_en_i;
  //   mem_control_bus_s[4:0] = {memory_access_en_i, byte_i, ldr_data_i, str_data_i, sel_mem_i}; sel_mem_s = sel_mem_i;
  //   str_data_s = str_data_i; ldr_data_s = ldr_data_i; byte_s = byte_i; memory_access_en_s = memory_access_en_i;
  //   reg_bank_control_bus_s[1:0] = {reg_bank_wr_i, reg_bank_en_i}; reg_bank_en_s = reg_bank_en_i;
  //   reg_bank_wr_s = reg_bank_wr_i

  // Notes on the sheet:
  //   Attention, votre version de Logisim
  //   ne contient pas de tracker. Si vous
  //   enregistrez votre projet, toutes les
  //   informations du tracker seront
  //   définitivement effacées.
endmodule

module Read_After_Write_detect (
  input  decode_en_i,
  input  [2:0] sel_rd_i,
  input  use_rd_i,
  input  [2:0] sel_rn_i,
  input  use_rn_i,
  input  [2:0] sel_rm_i,
  input  use_rm_i,
  input  [2:0] sel_rmem_i,
  input  use_rmem_i,
  input  clk_i,
  input  rst_i,
  output [2:0] sel_rd_o,
  output RAW_detected_o
);


  assign RAW_detected_o = 1'b0;
  assign sel_rd_o = 3'b000;

  // Other names for the same wires on the sheet: clk_s = clk_i; decode_en_s = decode_en_i; sel_rd_s[2:0] = sel_rd_i;
  //   sel_rm_s[2:0] = sel_rm_i; sel_rmem_s[2:0] = sel_rmem_i; sel_rn_s[2:0] = sel_rn_i; use_rd_s = use_rd_i;
  //   use_rm_s = use_rm_i; use_rmem_s = use_rmem_i; use_rn_s = use_rn_i

  // Notes on the sheet:
  //   Attention, votre version de Logisim
  //   ne contient pas de tracker. Si vous
  //   enregistrez votre projet, toutes les
  //   informations du tracker seront
  //   définitivement effacées.
endmodule

module bank_registers (
  input  reg_bank_en_i,
  input  clk_i,
  input  rst_i,
  input  [2:0] register_d_sel_i,
  input  [15:0] register_d_data_i,
  input  [2:0] register_n_sel_i,
  input  [2:0] register_m_sel_i,
  input  [2:0] register_mem_sel_i,
  input  [1:0] reg_bank_control_bus_i,
  input  [15:0] PC_fut_i,
  input  branch_i,
  input  link_en_i,
  output [15:0] register_n_read_data_o,
  output [15:0] register_m_read_data_o,
  output [15:0] register_mem_read_data_o,
  output [15:0] PC_pres_o
);


  assign PC_pres_o = {16{1'b0}};
  assign register_m_read_data_o = {16{1'b0}};
  assign register_mem_read_data_o = {16{1'b0}};
  assign register_n_read_data_o = {16{1'b0}};

  // Other names for the same wires on the sheet: bank_en_s = reg_bank_en_i; branch_s = branch_i; clk_s = clk_i;
  //   link_en_s = link_en_i; PC_fut_s[15:0] = PC_fut_i; reg_bank_control_bus[1:0] = reg_bank_control_bus_i;
  //   reg_d_sel_s[2:0] = register_d_sel_i; reg_m_sel_s[2:0] = register_m_sel_i;
  //   reg_mem_sel_s[2:0] = register_mem_sel_i; reg_n_sel_s[2:0] = register_n_sel_i;
  //   reg_write_data_s[15:0] = register_d_data_i; rst_s = rst_i

  // Notes on the sheet:
  //   Attention, votre version de Logisim
  //   ne contient pas de tracker. Si vous
  //   enregistrez votre projet, toutes les
  //   informations du tracker seront
  //   définitivement effacées.
  //   Banque de registres
endmodule

module LR_manager (
  input  [15:0] data_i,
  input  [15:0] pc_fut_lr_i,
  input  branch_i,
  input  write_en_i,
  input  link_en_i,
  output [15:0] LR_data_o,
  output LR_wr_en_o
);

  wire and_1_out;

  Multiplexer #(.width(16), .enable("false")) multiplexer_1 (
    .in0(data_i), .in1(pc_fut_lr_i), .out(LR_data_o), .sel(and_1_out));
  and and_1 (and_1_out, branch_i, link_en_i);
  or or_1 (LR_wr_en_o, write_en_i, link_en_i);

  // Notes on the sheet:
  //   Attention, votre version de Logisim
  //   ne contient pas de tracker. Si vous
  //   enregistrez votre projet, toutes les
  //   informations du tracker seront
  //   définitivement effacées.
endmodule

module execute (
  input  execute_en_i,
  input  [15:0] reg_data_n_i,
  input  [15:0] reg_data_m_i,
  input  [2:0] imm3,
  input  [4:0] imm5,
  input  [10:0] offset_incond,
  input  [7:0] offset_cond,
  input  [7:0] imm8,
  input  [14:0] execute_control_bus,
  input  rst_i,
  input  clk_i,
  output [15:0] data_out_o,
  output [3:0] cpsr_o
);


  assign cpsr_o = 4'b0000;
  assign data_out_o = {16{1'b0}};

  // Other names for the same wires on the sheet: clk_s = clk_i; execute_control_bus_s[14:0] = execute_control_bus;
  //   execute_en_s = execute_en_i; imm3_s[2:0] = imm3; imm5_s[4:0] = imm5; imm8_s[7:0] = imm8;
  //   offset_cond_s[7:0] = offset_cond; offset_incond_s[10:0] = offset_incond; reg_data_m_s[15:0] = reg_data_m_i;
  //   reg_data_n_s[15:0] = reg_data_n_i; rst_s = rst_i

  // Notes on the sheet:
  //   Attention, votre version de Logisim
  //   ne contient pas de tracker. Si vous
  //   enregistrez votre projet, toutes les
  //   informations du tracker seront
  //   définitivement effacées.
  //   Entité EXECUTE
endmodule

module mult_2 (
  input  [4:0] imm5_i,
  input  [10:0] offset_incond_i,
  input  [7:0] offset_cond_i,
  input  [2:0] sel_mult_2_i,
  output [15:0] mult_2_out
);

  wire [0:0] offset_cond_ext_signed_incr_x2_s;
  wire [15:0] imm5_ext_unsigned_s, imm5_ext_x2_s, offset_cond_ext_signed_incr_s, offset_cond_ext_signed_s,
       offset_incond_ext_signed_incr_s, offset_incond_ext_signed_incr_x2_s, offset_incond_ext_signed_s,
       offset_incond_ext_signed_shifted_incr_s, offset_incond_ext_signed_shifted_s,
       offset_incond_ext_unsigned_incr_s, offset_incond_ext_unsigned_incr_x2_s, offset_incond_ext_unsigned_s;
  wire [15:1] offset_cond_ext_signed_incr_aligned_s;

  assign imm5_ext_unsigned_s = {{11{1'b0}}, imm5_i};  // Bit_Extender bit_extender_1
  assign offset_incond_ext_signed_s = {{5{offset_incond_i[10]}}, offset_incond_i};  // Bit_Extender bit_extender_2
  assign offset_incond_ext_unsigned_s = {{5{1'b0}}, offset_incond_i};  // Bit_Extender bit_extender_3
  assign offset_cond_ext_signed_s = {{8{offset_cond_i[7]}}, offset_cond_i};  // Bit_Extender bit_extender_4
  Adder #(.width(16)) adder_1 (
    .a(offset_incond_ext_signed_s), .b(16'h2), .out(offset_incond_ext_signed_incr_s));  // open: cin, cout
  Adder #(.width(16)) adder_2 (
    .a(offset_cond_ext_signed_s), .b(16'h2), .out(offset_cond_ext_signed_incr_s));  // open: cin, cout
  Adder #(.width(16)) adder_3 (
    .a(offset_incond_ext_signed_shifted_s), .b(16'h2), .out(offset_incond_ext_signed_shifted_incr_s));  // open: cin, cout
  Adder #(.width(16)) adder_4 (
    .a(offset_incond_ext_unsigned_s), .b(16'h2), .out(offset_incond_ext_unsigned_incr_s));  // open: cin, cout
  Shifter #(.width(16)) shifter_1 (.in(imm5_ext_unsigned_s), .\dist (4'b0001), .out(imm5_ext_x2_s));
  Shifter #(.width(16)) shifter_2 (
    .in(offset_incond_ext_signed_incr_s), .\dist (4'b0001), .out(offset_incond_ext_signed_incr_x2_s));
  Shifter #(.width(16)) shifter_3 (
    .in(offset_cond_ext_signed_incr_s), .\dist (4'b0001),
    .out({offset_cond_ext_signed_incr_aligned_s, offset_cond_ext_signed_incr_x2_s[0]}));
  Shifter #(.width(16)) shifter_4 (
    .in(offset_incond_ext_unsigned_incr_s), .\dist (4'b0001), .out(offset_incond_ext_unsigned_incr_x2_s));
  Shifter #(.width(16)) shifter_5 (
    .in(offset_incond_ext_signed_s), .\dist (4'b1100), .out(offset_incond_ext_signed_shifted_s));
  Multiplexer #(.select(3), .width(16), .enable("false")) multiplexer_1 (
    .in0(imm5_ext_x2_s), .in1(offset_incond_ext_signed_incr_x2_s),
    .in2({offset_cond_ext_signed_incr_aligned_s, 1'b0}), .in3(offset_incond_ext_unsigned_incr_x2_s),
    .in4(imm5_ext_unsigned_s), .in5(offset_incond_ext_signed_shifted_s), .in6(offset_incond_ext_unsigned_s),
    .in7({16{1'b0}}), .out(mult_2_out), .sel(sel_mult_2_i));

  // Other names for the same wires on the sheet: imm5_s[4:0] = imm5_i; mult_2_out_s[15:0] = mult_2_out;
  //   offset_cond_ext_signed_incr_x2_s[15:1] = offset_cond_ext_signed_incr_aligned_s;
  //   offset_cond_s[7:0] = offset_cond_i; offset_incond_s[10:0] = offset_incond_i; sel_mult_2_s[2:0] = sel_mult_2_i

  // Notes on the sheet:
  //   Attention, votre version de Logisim
  //   ne contient pas de tracker. Si vous
  //   enregistrez votre projet, toutes les
  //   informations du tracker seront
  //   définitivement effacées.
  //   Extensions nécessaires
  //   Incréments
  //   x2 => shift à gauche = pas de logique
  //   Utilisé pour le BL MSB
  //   Utilisé pour le BL LSB (or logique)
endmodule

module shift (
  input  [15:0] operand_i,
  input  [3:0] sel_shift_data_i,
  input  [2:0] sel_op_shift_i,
  output [15:0] shift_data_out_o
);


  assign shift_data_out_o = {16{1'b0}};

  // Other names for the same wires on the sheet: operand_s[15:0] = operand_i; sel_op_shift_s[2:0] = sel_op_shift_i;
  //   sel_shift_data_s[3:0] = sel_shift_data_i

  // Notes on the sheet:
  //   Attention, votre version de Logisim
  //   ne contient pas de tracker. Si vous
  //   enregistrez votre projet, toutes les
  //   informations du tracker seront
  //   définitivement effacées.
endmodule

module alu (
  input  [15:0] operand_1_i,
  input  [15:0] operand_2_i,
  input  [2:0] sel_op_alu_i,
  output [15:0] alu_data_out_o,
  output carry_o,
  output overflow_o
);


  assign alu_data_out_o = {16{1'b0}};
  assign carry_o = 1'b0;
  assign overflow_o = 1'b0;

  // Other names for the same wires on the sheet: operand_1_s[15:0] = operand_1_i; operand_2_s[15:0] = operand_2_i;
  //   sel_op_alu_s[2:0] = sel_op_alu_i

  // Notes on the sheet:
  //   Attention, votre version de Logisim
  //   ne contient pas de tracker. Si vous
  //   enregistrez votre projet, toutes les
  //   informations du tracker seront
  //   définitivement effacées.
endmodule

module zcnv_unit (
  input  [15:0] data_i,
  input  carry_i,
  input  overflow_i,
  output z_o,
  output c_o,
  output n_o,
  output v_o
);


  assign c_o = 1'b0;
  assign n_o = 1'b0;
  assign v_o = 1'b0;
  assign z_o = 1'b0;

  // Other names for the same wires on the sheet: carry_s = carry_i; data_s[15:0] = data_i; overflow_s = overflow_i

  // Notes on the sheet:
  //   Attention, votre version de Logisim
  //   ne contient pas de tracker. Si vous
  //   enregistrez votre projet, toutes les
  //   informations du tracker seront
  //   définitivement effacées.
endmodule

module memory_access (
  input  memory_access_en_i,
  input  [15:0] mem_data_i,
  input  [15:0] reg_data_i,
  input  [15:0] data_i,
  input  [4:0] memory_control_bus_i,
  input  rst_i,
  input  clk_i,
  output [14:0] mem_data_adr_o,
  output [15:0] mem_adr_byte_o,
  output [15:0] mem_data_out_o,
  output [15:0] mem_out_o,
  output str_data_o,
  output ldr_data_o,
  output high_byte_o,
  output low_byte_o
);


  assign high_byte_o = 1'b0;
  assign ldr_data_o = 1'b0;
  assign low_byte_o = 1'b0;
  assign mem_adr_byte_o = {16{1'b0}};
  assign mem_data_adr_o = {15{1'b0}};
  assign mem_data_out_o = {16{1'b0}};
  assign mem_out_o = {16{1'b0}};
  assign str_data_o = 1'b0;

  // Other names for the same wires on the sheet: data_s[15:0] = data_i; mem_data_s[15:0] = mem_data_i;
  //   memory_access_en_s = memory_access_en_i; memory_control_bus_s[4:0] = memory_control_bus_i;
  //   reg_data_s[15:0] = reg_data_i

  // Notes on the sheet:
  //   Attention, votre version de Logisim
  //   ne contient pas de tracker. Si vous
  //   enregistrez votre projet, toutes les
  //   informations du tracker seront
  //   définitivement effacées.
  //   Entité MEMORY ACCESS
endmodule

module controller_pipeline (
  input  RAW_detected_i,
  input  branch_i,
  input  cond_en_i,
  input  clk_i,
  input  rst_i,
  output fetch_en_o,
  output decode_en_o,
  output reg_bank_en_o,
  output execute_en_o,
  output memory_access_o
);


  assign decode_en_o = 1'b1;
  assign execute_en_o = 1'b1;
  assign fetch_en_o = 1'b1;
  assign memory_access_o = 1'b1;
  assign reg_bank_en_o = 1'b1;

  // Other names for the same wires on the sheet: branch_s = branch_i; clk_s = clk_i; RAW_detected_s = RAW_detected_i;
  //   rst_s = rst_i

  // Notes on the sheet:
  //   Attention, votre version de Logisim
  //   ne contient pas de tracker. Si vous
  //   enregistrez votre projet, toutes les
  //   informations du tracker seront
  //   définitivement effacées.
endmodule

module is_conditional (
  input  [15:0] inst_addr_i,
  output is_conditional
);

  Comparator #(.width(4)) comparator_1 (.a(inst_addr_i[15:12]), .b(4'b1101), .eq(is_conditional));  // open: gt, lt

  // Notes on the sheet:
  //   Attention, votre version de Logisim
  //   ne contient pas de tracker. Si vous
  //   enregistrez votre projet, toutes les
  //   informations du tracker seront
  //   définitivement effacées.
endmodule

module is_unconditional (
  input  [15:0] inst_addr_i,
  output is_unconditional
);

  Comparator #(.width(5)) comparator_1 (.a(inst_addr_i[15:11]), .b(5'b11100), .eq(is_unconditional));  // open: gt, lt

  // Notes on the sheet:
  //   Attention, votre version de Logisim
  //   ne contient pas de tracker. Si vous
  //   enregistrez votre projet, toutes les
  //   informations du tracker seront
  //   définitivement effacées.
endmodule

module offset_inconditional (
  input  [15:0] instr_address_i,
  input  [15:0] PC_pres_i,
  output [15:0] branch_address_o
);

  wire [15:0] adder_1_out;

  Adder #(.width(16)) adder_1 (
    .a({{5{instr_address_i[10]}}, instr_address_i[9:0], 1'b0}), .b(PC_pres_i), .out(adder_1_out));  // open: cin, cout
  Adder #(.width(16)) adder_2 (.a(adder_1_out), .b(16'h4), .out(branch_address_o));  // open: cin, cout

  // Other names for the same wires on the sheet: address[15:0] = instr_address_i; PC_pres[15:0] = PC_pres_i

  // Notes on the sheet:
  //   Attention, votre version de Logisim
  //   ne contient pas de tracker. Si vous
  //   enregistrez votre projet, toutes les
  //   informations du tracker seront
  //   définitivement effacées.
endmodule

module offset_conditional (
  input  [15:0] instr_add_i,
  input  [15:0] PC_pres_i,
  output [15:0] branch_address_o
);

  wire [15:0] adder_1_out;

  Adder #(.width(16)) adder_1 (
    .a({{8{instr_add_i[7]}}, instr_add_i[6:0], 1'b0}), .b(PC_pres_i), .out(adder_1_out));  // open: cin, cout
  Adder #(.width(16)) adder_2 (.a(adder_1_out), .b(16'h4), .out(branch_address_o));  // open: cin, cout

  // Other names for the same wires on the sheet: address[15:0] = instr_add_i; PC_pres[15:0] = PC_pres_i

  // Notes on the sheet:
  //   Attention, votre version de Logisim
  //   ne contient pas de tracker. Si vous
  //   enregistrez votre projet, toutes les
  //   informations du tracker seront
  //   définitivement effacées.
endmodule
